# Fritzing sketch arduino_LCD_RTC_SD (saved by Fritzing 0.9.2b)

parts:
  Part1 = Arduino Mega 2560 (Rev3)
  Part2 = Real Time Clock Module - DS1307 RTC Breakout Board
  microSD2 = MicroSD Breakout
  U3 = LCD-16X2 [package=lcd-16x2]
  U4 = POT [package=pot_mammoth]

nets (from the breadboard view):
  N1: Part1.D21/SCL, Part1.SCL, Part2.SCL
  N2: Part1.D20/SDA, Part1.SDA, Part2.SDA
  GND: Part1.GND, Part2.GND, microSD2.GND, U3.VSS, U3.R_W, U3.K, U4.S
  N3: Part1.D12_PWM, U3.RS
  N4: Part1.D11_PWM, U3.E, U3.DB0, U3.DB1
  5V: Part1.5V, Part2.5V, microSD2.5V, U3.VDD, U4.E
  N5: Part1.D2_PWM, U3.DB7
  N6: Part1.D3_PWM, U3.DB6
  N7: Part1.D4_PWM, U3.DB5
  N8: Part1.D5_PWM, U3.DB3, U3.DB4
  N9: Part1.D50, microSD2.DO
  N10: Part1.D51, microSD2.DI
  N11: Part1.D52, microSD2.CLK
  N12: Part1.D53, microSD2.CS
  N13: U3.VO, U4.A

custom parts:
  MicroSD Breakout: 5V-ready microSD Breakout with Level Shifter
